# Fritzing sketch Perfboard Layout (saved by Fritzing 0.9.3b)
perfboards: 1

parts:
  Part1 = NRF24L01+ Breakout Board  # not connected
  Part2 = Arduino Nano (Rev3.0)  # not connected
  Q1 = Basic FET P-Channel [package="TO220 [THT]"]  # not connected
  Q2 = Basic FET P-Channel [package="TO220 [THT]"]  # not connected
  Q3 = Basic FET P-Channel [package="TO220 [THT]"]  # not connected
  Power_plug1 = Power plug
  J1 = female pin header, 15 pins [form="♀ (female)"]  # not connected
  J2 = female pin header, 15 pins [form="♀ (female)"]  # not connected
  J3 = female pin header, 4 pins [form="♀ (female)"]  # not connected
  J4 = female pin header, 4 pins [form="♀ (female)"]  # not connected
  JP1 = Header 4 [package=jst-4-pth]  # not connected
  JP2 = Header 2 [package=r_sw_th]

nets:
  N1: Power_plug1.VCC, JP2.1
